# Fritzing sketch ledcontrol-WS281X (saved by Fritzing 0.9.4)

parts:
  Raspberry_Pi_1 = Raspberry Pi 3 [part_number=RPI-3-V1.2]
  Bauteil2 = Adafruit 4-channel I2C-safe Bi-directional Logic Level Converter [part_number="Adafruit #757"]
  NEOPIXEL1 = Neopixel Strip -- White (60/m) [part_number=1138]

nets:
  N1: Raspberry_Pi_1.3v3, Bauteil2.LV
  N2: Raspberry_Pi_1.GIPO21, Bauteil2.A1
  N3: Bauteil2.B1, NEOPIXEL1.DO

notes:
  220AC to 5V DC Converter
  AC 220V DC 5V
  N P L V+ V-

custom parts:
  Adafruit 4-channel I2C-safe Bi-directional Logic Level Converter: Because the Arduino (and Basic Stamp) are 5V devices, and most modern sensors, displays, flash cards and modes are 3.3V-only, many makers find that they need to perform level shifting/conversion to protect the 3.3V device from 5V. We do have some other handy level shifters in the shop, from the DIP 74LVC245 to the fancy bi-directional TXB0108. However, neither of these are happy to work with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
  Neopixel Strip -- White (60/m): Neopixel Strip, White, 60 pixels per meter.
