# Fritzing sketch ledcontrol-buttons-pulldown (saved by Fritzing 0.9.4)

parts:
  Raspberry_Pi_1 = Raspberry Pi 3 [part_number=RPI-3-V1.2]
  S1 = Pushbutton [package="[THT]"]
  S2 = Pushbutton [package="[THT]"]
  R1 = Resistor [tolerance=±5% resistance=2.2k package=THT]
  R2 = Resistor [tolerance=±5% resistance=2.2k package=THT]

nets:
  N1: Raspberry_Pi_1.GIPO17, S1.Pin_2
  N2: Raspberry_Pi_1.GIPO27, S2.Pin_2
  N3: Raspberry_Pi_1.3V3, S2.Pin_3, S2.Pin_4
  N4: Raspberry_Pi_1.GND, R1.Pin_0, R2.Pin_0
