# Fritzing sketch ledcontrol-buttons-pullup-withCapacitors (saved by Fritzing 0.9.3b)

parts:
  Raspberry_Pi_1 = Raspberry Pi 3 [part_number=RPI-3-V1.2]
  S1 = Pushbutton [package="[THT]"]
  S2 = Pushbutton [package="[THT]"]
  R1 = Resistor [tolerance=±5% resistance=10k package=THT]  # not connected
  R2 = Resistor [tolerance=±5% resistance=10k package=THT]
  C2 = Electrolytic Capacitor [capacitance=100μF package="0807 [SMD, electrolytic]"]  # not connected
  C3 = Electrolytic Capacitor [capacitance=100μF package="0807 [SMD, electrolytic]"]  # not connected

nets:
  N1: Raspberry_Pi_1.GIPO17, S1.Pin_2
  N2: Raspberry_Pi_1.GIPO27, S2.Pin_2
  N3: Raspberry_Pi_1.3V3, R2.Pin_0
  N4: Raspberry_Pi_1.GND, S2.Pin_3, S2.Pin_4

notes:
  Both Capacitors
  are 0.1 μF (100nF)
