# Fritzing sketch ledcontrol (saved by Fritzing 0.9.3b)

parts:
  Raspberry_Pi_1 = Raspberry Pi 3 [part_number=RPI-3-V1.2]
  DOTSTAR1 = DotStar Strip -- White (60/m) [part_number=2240]
  S1 = Pushbutton [package="[THT]"]
  S2 = Pushbutton [package="[THT]"]
  Bauteil2 = Adafruit 4-channel I2C-safe Bi-directional Logic Level Converter [part_number="Adafruit #757"]
  R1 = Resistor [tolerance=±5% resistance=2.2k package=THT]
  R2 = Resistor [tolerance=±5% resistance=2.2k package=THT]  # not connected

nets:
  N1: Raspberry_Pi_1.3v3, Bauteil2.LV
  N2: Raspberry_Pi_1.GIPO17, S1.Pin_2
  N3: Raspberry_Pi_1.GIPO27, S2.Pin_2
  GND: Raspberry_Pi_1.GND, Bauteil2.GND, R1.Pin_0
  N4: DOTSTAR1.DI, Bauteil2.B2
  N5: DOTSTAR1.CI, Bauteil2.B1

notes:
  220AC to 5V DC Converter
  AC 220V DC 5V
  N P L V+ V-

custom parts:
  DotStar Strip -- White (60/m): NeopixelDotStar Strip, White, 60 pixels per meter.
  Adafruit 4-channel I2C-safe Bi-directional Logic Level Converter: Because the Arduino (and Basic Stamp) are 5V devices, and most modern sensors, displays, flash cards and modes are 3.3V-only, many makers find that they need to perform level shifting/conversion to protect the 3.3V device from 5V. We do have some other handy level shifters in the shop, from the DIP 74LVC245 to the fancy bi-directional TXB0108. However, neither of these are happy to work with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
